# Fritzing sketch SEGUIDOR US LINEAL (saved by Fritzing 0.9.3b)
breadboards: 1

parts:
  hc-sr1 = hc-sr04
  Componente1 = Arduino Uno (Rev3)
  M2 = DC Motor
  J1 = Piezo Speaker
  U1 = L9110 H-bridge module [part_number="L9110 H-bridge"]

nets:
  VCC: hc-sr1.VCC, Componente1.5V, U1.VCC
  N1: hc-sr1.Trig, Componente1.D4
  N2: hc-sr1.Echo, Componente1.D3_PWM
  GND: hc-sr1.GND, Componente1.GND, J1.pin1, U1.GND
  N3: Componente1.D11_PWM/MOSI, U1.A-IB
  N4: Componente1.D12/MISO, U1.A-IA
  N5: Componente1.D2, J1.pin2
  N6: M2.pin_1, U1.MOTOR_B-B
  N7: M2.pin_2, U1.MOTOR_B-A
